// Logisim project main.circ as structural Verilog
module ALU (
  input  [7:0] A,
  input  [7:0] B,
  input  [7:0] OPCODE,
  input  [7:0] In_flags,
  output [7:0] Out,
  output [3:0] Out_flags
);

  wire adder_1_cout, subtractor_1_bout;
  wire [7:0] adder_1_out, subtractor_1_out;

  Adder adder_1 (.a(A), .b(B), .out(adder_1_out), .cin(In_flags[0]), .cout(adder_1_cout));
  Subtractor subtractor_1 (.a(A), .b(B), .out(subtractor_1_out), .bin(In_flags[0]), .bout(subtractor_1_bout));
  Multiplexer #(.select(4), .enable("false")) multiplexer_1 (
    .in0(adder_1_cout), .in1(subtractor_1_bout), .out(Out_flags[0]), .sel(OPCODE[3:0]));  // open: in2, in3, in4, in5, in6, in7, in8, in9, in10, in11, in12, in13, in14, in15
  Multiplexer #(.select(4), .width(8), .enable("false")) multiplexer_2 (
    .in0(adder_1_out), .in1(subtractor_1_out), .out(Out), .sel(OPCODE[3:0]));  // open: in2, in3, in4, in5, in6, in7, in8, in9, in10, in11, in12, in13, in14, in15
  Pull_Resistor pull_resistor_1 (.node(Out_flags[3]));

  assign Out_flags[2:1] = {2{Out_flags[3]}};

  // Other names for the same wires on the sheet: Carry_in = In_flags[0]

  // Notes on the sheet:
  //   ALU interface
  //   - carry out$- overflow$- zero$- negative
endmodule
